# Fritzing sketch 7404 (1) (saved by Fritzing 0.9.4)
breadboards: 1

parts:
  VCC1 = Battery
  LED1 = LED - 5mm [color="Red (633nm)" package="5 mm [THT]"]
  U1 = SN74LS14N [package="DIP14 [THT]"]

nets:
  N1: VCC1.-, LED1.cathode
  N2: VCC1.+, U1.6A, U1.VCC
  N3: LED1.anode, U1.3Y, U1.GND
  N4: U1.1A, U1.4Y
  N5: U1.1Y, U1.2A
  N6: U1.2Y, U1.3A
  N7: U1.4A, U1.5Y
  N8: U1.5A, U1.6Y
