# Fritzing sketch LED (saved by Fritzing 0.9.4)
breadboards: 1

parts:
  VCC1 = Battery
  LED1 = LED - 5mm [color="Red (633nm)" package="5 mm [THT]"]
  R1 = Resistor [tolerance=±5% resistance=220 package=THT]

nets:
  N1: VCC1.-, LED1.cathode
  N2: VCC1.+, R1.Pin_0
  N3: LED1.anode, R1.Pin_1
