// Logisim project add and sub.circ as structural Verilog: 1 circuit, main circuit main
module main (
  input  A4,
  input  A3,
  input  A2,
  input  A1,
  input  B4,
  input  B3,
  input  B2,
  input  B1,
  input  Cin,
  output S4,
  output S3,
  output S2,
  output S1
);

  wire main_2_c_out, main_3_c_out, main_4_c_out, xor_1_out, xor_2_out, xor_3_out, xor_4_out;

  xor xor_1 (xor_1_out, B4, Cin);
  _4bit_FULLaDDER_main main_1 (.C(main_2_c_out), .A(A4), .B(xor_1_out), .S(S4));  // open: C_out
  xor xor_2 (xor_2_out, B3, Cin);
  _4bit_FULLaDDER_main main_2 (.C(main_3_c_out), .A(A3), .B(xor_2_out), .S(S3), .C_out(main_2_c_out));
  xor xor_3 (xor_3_out, B2, Cin);
  _4bit_FULLaDDER_main main_3 (.C(main_4_c_out), .A(A2), .B(xor_3_out), .S(S2), .C_out(main_3_c_out));
  xor xor_4 (xor_4_out, B1, Cin);
  _4bit_FULLaDDER_main main_4 (.C(Cin), .A(A1), .B(xor_4_out), .S(S1), .C_out(main_4_c_out));
endmodule
